// Digital circuit CPU.dig as structural Verilog
module CPU (
  input  [7:0] Input,
  input  _1Hz,
  input  _100Hz,
  output [7:0] Output
);

  wire and_1_out, and_2_out, and_3_out, and_4_out, and_5_out, and_7_out, and_8_out, and_9_out, and_10_out,
       and_11_out, and_12_out, and_13_out, and_14_out, and_15_out, and_16_out, and_25_out, and_26_out,
       and_27_out, and_28_out, and_29_out, and_30_out, and_32_out, and_34_out, and_35_out, and_36_out,
       button_1_out, buttonled_1_p1, buttonled_1_p2, buttonled_2_p1, buttonled_2_p2, buttonled_3_p1,
       buttonled_3_p2, Clk, Data_Str, DepthsMatch, dipswitch_1_out, Dir, Enable, EndOfAddr, nand_1_out, nClk,
       nCntr_Clr, nInput_Await, NonZero, nor_1_out, nor_2_out, nor_3_out, nor_4_out, nor_5_out, nor_6_out,
       not_1_out, not_3_out, not_4_out, not_5_out, nPntr_Clr, nReset_out, nRst, nSeek, nSeekTrigger,
       nStep_Rst, or_1_out, or_2_out, or_6_out, or_7_out, or_8_out, or_9_out, or_10_out, or_11_out,
       or_12_out, Pulse_out, rs_ff_as_1_q, rs_ff_as_4_nq, rs_ff_as_4_q, rs_ff_as_5_q, rs_ff_as_7_nq,
       rs_ff_as_7_q, rs_ff_as_8_q, rs_ff_as_9_nq, rs_ff_as_9_q, Rst, Seek, SeekTrigger, Send_out, xor_3_out;
  wire [2:0] Step;
  wire [3:3] counter4_1_out;
  wire [7:0] Changer_p7, counter16_1_out, counter16_1_out_2, Data, not_2_out, register8_1_q, register8_2_q,
       rom_1_d, uCode_A_d, uCode_B_d;
  wire [11:4] and_24_out;
  wire [15:0] Addr, ProgAddr;

  DipSwitch #(.dipDefault("true")) nReset (.out(nReset_out));
  and and_1 (and_1_out, or_1_out, Clk);
  and and_2 (and_2_out, Clk, rs_ff_as_5_q);
  not not_1 (not_1_out, nReset_out);
  and and_3 (and_3_out, nReset_out, nClk);
  RS_FF_AS rs_ff_as_1 (.S(and_1_out), .R(and_2_out), .Q(rs_ff_as_1_q));  // open: nQ
  RS_FF_AS rs_ff_as_2 (.S(and_2_out), .R(Rst), .Q(Enable));  // open: nQ
  RS_FF_AS rs_ff_as_3 (.S(Rst), .R(rs_ff_as_5_q), .Q(Data_Str));  // open: nQ
  RS_FF_AS rs_ff_as_4 (.S(not_1_out), .R(and_3_out), .Q(rs_ff_as_4_q), .nQ(rs_ff_as_4_nq));
  and and_4 (and_4_out, rs_ff_as_4_nq, Clk);
  and and_5 (and_5_out, nClk, rs_ff_as_1_q);
  RS_FF_AS rs_ff_as_5 (.S(and_5_out), .R(and_2_out), .Q(rs_ff_as_5_q), .nQ(nCntr_Clr));
  RS_FF_AS rs_ff_as_6 (.S(rs_ff_as_4_q), .R(and_4_out), .Q(Rst), .nQ(nRst));
  and and_6 (nPntr_Clr, nCntr_Clr, nRst);
  LED led_1 (.in(Clk));
  LED led_2 (.in(Rst));
  LED led_3 (.in(nCntr_Clr));
  LED led_4 (.in(nPntr_Clr));
  LED led_5 (.in(EndOfAddr));
  LED led_6 (.in(Data_Str));
  LED led_7 (.in(Data_Str));
  LED led_8 (.in(Enable));
  or or_1 (or_1_out, dipswitch_1_out, EndOfAddr);
  DipSwitch dipswitch_1 (.out(dipswitch_1_out));
  or or_2 (or_2_out, and_2_out, buttonled_1_p1);
  // ButtonLED buttonled_1: pin names not known; wires that end beside it: buttonled_1_p1, buttonled_1_p2
  // ButtonLED buttonled_2: pin names not known; wires that end beside it: buttonled_2_p1, buttonled_2_p2
  // ButtonLED buttonled_3: pin names not known; wires that end beside it: buttonled_3_p1, buttonled_3_p2
  nor nor_1 (nor_1_out, buttonled_2_p2, buttonled_3_p2);
  nor nor_2 (nor_2_out, buttonled_1_p2, buttonled_3_p2);
  nor nor_3 (nor_3_out, buttonled_1_p2, buttonled_2_p2);
  or or_3 (buttonled_1_p2, or_2_out, nor_1_out);
  or or_4 (buttonled_2_p2, buttonled_2_p1, nor_2_out);
  or or_5 (buttonled_3_p2, buttonled_3_p1, nor_3_out);
  assign not_2_out = ~rom_1_d;  // Not not_2, 8 bits wide
  Button Pulse (.out(Pulse_out));
  and and_7 (and_7_out, rom_1_d[0], rom_1_d[1], not_2_out[2], rom_1_d[3]);
  and and_8 (and_8_out, rom_1_d[0], not_2_out[1], rom_1_d[2], rom_1_d[3]);
  and and_9 (and_9_out, not_2_out[0], not_2_out[1], rom_1_d[2], rom_1_d[3]);
  and and_10 (and_10_out, not_2_out[0], rom_1_d[1], rom_1_d[2], rom_1_d[3]);
  and and_11 (and_11_out, not_2_out[4], rom_1_d[5], not_2_out[6], not_2_out[7]);
  and and_12 (and_12_out, rom_1_d[4], rom_1_d[5], not_2_out[6], not_2_out[7]);
  and and_13 (and_13_out, rom_1_d[4], not_2_out[5], rom_1_d[6], not_2_out[7]);
  and and_14 (and_14_out, buttonled_1_p2, Pulse_out);
  and and_15 (and_15_out, buttonled_2_p2, _1Hz);
  and and_16 (and_16_out, buttonled_3_p2, _100Hz);
  ROM #(.AddrBits(16), .Bits(8)) rom_1 (.A(ProgAddr), .sel(1'b1), .D(rom_1_d));
  or or_6 (or_6_out, and_14_out, or_7_out);
  or or_7 (or_7_out, and_15_out, and_16_out);
  and and_17 (and_24_out[4], and_7_out, and_11_out);
  and and_18 (and_24_out[5], and_8_out, and_11_out);
  and and_19 (and_24_out[6], and_9_out, and_11_out);
  and and_20 (and_24_out[7], and_10_out, and_11_out);
  and and_21 (and_24_out[8], and_9_out, and_12_out);
  and and_22 (and_24_out[9], and_12_out, and_10_out);
  and and_23 (and_24_out[10], and_13_out, and_7_out);
  and and_24 (and_24_out[11], and_8_out, and_13_out);
  LED led_9 (.in(or_6_out));
  LED plus (.in(and_24_out[4]));
  LED led_10 (.in(and_24_out[5]));
  LED led_11 (.in(and_24_out[6]));
  LED led_12 (.in(and_24_out[7]));
  LED lt (.in(and_24_out[8]));
  LED gt (.in(and_24_out[9]));
  LED led_13 (.in(and_24_out[10]));
  LED led_14 (.in(and_24_out[11]));
  xor xor_1 (Clk, or_6_out, 1'b0);
  xor xor_2 (nClk, or_6_out, 1'b1);
  not not_3 (not_3_out, Enable);
  Counter4 counter4_1 (
    .nPL(nStep_Rst), .nU_D(1'b0), .CP(nClk), .nCE(not_3_out), .In(4'b0000), .Out({counter4_1_out[3], Step}));  // open: nRC
  // Probe on Step
  ROM #(.AddrBits(12), .Bits(8)) uCode_A (.A({and_24_out, Step, Enable}), .sel(1'b1), .D(uCode_A_d));
  ROM #(.AddrBits(12), .Bits(8)) uCode_B (.A({and_24_out, Step, Enable}), .sel(1'b1), .D(uCode_B_d));
  LED Output_In (.in(uCode_B_d[4]));
  LED TrySeek (.in(uCode_B_d[3]));
  LED TryStopSeek (.in(uCode_B_d[2]));
  LED TryLatchDepth (.in(uCode_B_d[1]));
  LED CountDepth (.in(uCode_B_d[0]));
  LED Input_Await (.in(uCode_B_d[6]));
  LED Input_Out (.in(uCode_B_d[5]));
  LED Data_In (.in(uCode_A_d[0]));
  LED Data_Out (.in(uCode_B_d[7]));
  LED Counter_Cnt (.in(uCode_A_d[7]));
  LED Pointer_Inc (.in(uCode_A_d[6]));
  LED Pointer_Dec (.in(uCode_A_d[5]));
  LED Changer_Add (.in(uCode_A_d[4]));
  LED Changer_Sub (.in(uCode_A_d[3]));
  LED Changer_In (.in(uCode_A_d[2]));
  LED Changer_Out (.in(uCode_A_d[1]));
  // Probe Counter_Cnt on uCode_A_d[7]
  RS_FF_AS rs_ff_as_7 (.S(uCode_B_d[6]), .R(and_30_out), .Q(rs_ff_as_7_q), .nQ(rs_ff_as_7_nq));
  and and_25 (and_25_out, uCode_B_d[3], SeekTrigger);
  or or_8 (or_8_out, rs_ff_as_7_nq, Rst);
  and and_26 (and_26_out, uCode_B_d[2], DepthsMatch);
  xor xor_3 (xor_3_out, and_24_out[11], Dir);
  and and_27 (and_27_out, Clk, rs_ff_as_7_q);
  or or_9 (or_9_out, Rst, and_26_out);
  and and_28 (and_28_out, and_25_out, and_24_out[11]);
  and and_29 (and_29_out, xor_3_out, nSeekTrigger);
  Button button_1 (.out(button_1_out));
  nor nor_4 (nor_4_out, uCode_A_d[3], uCode_A_d[4]);
  nor nor_5 (nor_5_out, uCode_A_d[2], Rst);
  RS_FF_AS rs_ff_as_8 (.S(and_27_out), .R(or_8_out), .Q(rs_ff_as_8_q), .nQ(nInput_Await));
  and and_30 (and_30_out, Clk, Send_out);
  and and_31 (nStep_Rst, nRst, rs_ff_as_9_nq);
  RS_FF_AS rs_ff_as_9 (.S(uCode_A_d[7]), .R(button_1_out), .Q(rs_ff_as_9_q), .nQ(rs_ff_as_9_nq));
  JK_FF jk_ff_1 (.J(and_25_out), .C(~nClk), .K(or_9_out), .Q(Seek), .nQ(nSeek));
  JK_FF jk_ff_2 (.J(and_28_out), .C(~nClk), .K(or_9_out), .Q(Dir));  // open: nQ
  and and_32 (and_32_out, nSeek, SeekTrigger);
  Counter16 counter16_1 (
    .nPL(Rst), .nU_D(and_29_out), .CP(Clk), .nCE(uCode_B_d[0]), .In({16{1'b0}}),
    .Out({counter16_1_out_2, counter16_1_out}));  // open: nRC
  Counter16 Counter (
    .nPL(nCntr_Clr), .nU_D(Dir), .CP(nClk), .nCE(rs_ff_as_9_nq), .In({16{1'b0}}), .Out(ProgAddr));  // open: nRC
  // Counter8 Changer: pin names not known; wires that end beside it: rs_ff_as_9_q, nor_5_out, uCode_A_d[3], Clk, nor_4_out, Data, Changer_p7
  LED led_15 (.in(rs_ff_as_8_q));
  Button Send (.out(Send_out));
  assign Data = uCode_B_d[5] ? Input : 8'bz;  // Driver driver_1
  LED u_Seek (.in(Seek));
  LED u_Dir (.in(Dir));
  nand nand_1 (nand_1_out, and_32_out, uCode_B_d[1]);
  assign Data = uCode_A_d[1] ? Changer_p7 : 8'bz;  // Driver driver_2
  Register8 register8_1 (.nEn(nand_1_out), .D(counter16_1_out), .Clk(Clk), .Q(register8_1_q));
  Register8 register8_2 (.nEn(nand_1_out), .D(counter16_1_out_2), .Clk(Clk), .Q(register8_2_q));
  or or_10 (or_10_out, uCode_A_d[6], uCode_A_d[5]);
  not not_4 (not_4_out, uCode_B_d[4]);
  nor nor_6 (nor_6_out, Data_Str, or_10_out);
  or or_11 (or_11_out, uCode_A_d[0], Data_Str);
  not not_5 (not_5_out, NonZero);
  and and_33 (SeekTrigger, or_12_out, nSeek);
  Equal equal_1 (.A({register8_2_q, register8_1_q}), .B({counter16_1_out_2, counter16_1_out}), .Eq(DepthsMatch));
  Counter16 Pointer (
    .nPL(nPntr_Clr), .nU_D(uCode_A_d[5]), .CP(Clk), .nCE(nor_6_out), .In({16{1'b0}}), .Out(Addr));  // open: nRC
  RAMDualPort #(.AddrBits(16), .Bits(8)) u_Data (
    .A(Addr), .Din(Data), .str(or_11_out), .C(Clk), .ld(uCode_B_d[7]), .D(Data));
  PullDown #(.Bits(8)) pulldown_1 (.out(Data));
  and and_34 (and_34_out, uCode_B_d[4], Clk);
  Register8 register8_3 (.nEn(not_4_out), .D(Data), .Clk(Clk), .Q(Output));
  and and_35 (and_35_out, and_24_out[11], NonZero);
  and and_36 (and_36_out, not_5_out, and_24_out[10]);
  not not_6 (nSeekTrigger, SeekTrigger);
  // Probe on Addr
  // Probe on Data
  LED led_16 (.in(and_34_out));
  or or_12 (or_12_out, and_35_out, and_36_out);
  // Probe on {register8_2_q, register8_1_q}
  // Probe on {counter16_1_out_2, counter16_1_out}
  EndOfAddress endofaddress_1 (.D(Addr), .End(EndOfAddr));
  Nonzero nonzero_1 (.D(Data), .NZ(NonZero));
  LED Seek_Trigger (.in(SeekTrigger));

  // Other names for the same wires on the sheet: Pntr_Up = Data_Str

  // Notes on the sheet:
  //   _100Hz: Hz: 100
  //   Reset Timing
  //   Data Wipe Sequencing
  //   RAM chip connections:
  //   ~WE = Data_In NAND +Clk
  //   ~OE = DATA_Out
  //   ~CS = 0
  //   Alternatively:
  //   LowerRAM.~CS = A_15
  //   UpperRAM.~CS = NOT A_15
  //   EndOfAddress goes
  //   high on -Clk when
  //   the wiping process is complete
  //   EndOfAddress will be
  //   determined by the value
  //   of Cntr
  //   Wire colors:
  //   Clock lines - yellow
  //   Step lines/logic - red
  //   Decoding logic - green
  //   Decision logic - blue
  //   Manupulation logic - white
  //   Signal Display
  //   Clock Generation
  //   Decode
  //   rom_1 loads program.bf
  //   Control Microcode
  //   uCode_A loads ucodeA.bin
  //   uCode_B loads ucodeB.bin
  //   Seek/Dir Latching
  //   Input
  //   Depth Comparison
  //   Counter
  //   Data Changer
  //   Depth
  //   Pointer
  //   Data
  //   Output
  //   Seek Trigger
  //   Target Depth
  //   Current Depth
endmodule
